# Fritzing sketch Pulse1_wTooGoo (saved by Fritzing 0.9.3b)
circuit board: 9.00001cm x 5.99999cm
breadboards: 1

parts:
  RESET = Momentary Switch [package=tactile-pth]
  TrimPot = Trimmer Potentiometer [maximum_resistance=10kΩ package=THT]
  NANO = Arduino Nano (Rev3.0)
  BATT = female pin header, 2 pins [form="♀ (female)"]
  INK1 = Nokia 5110 [part_number="Nokia 5110"]
  LED_BLINK = female pin header, 2 pins [form="♀ (female)"]
  SW1 = Slide_Switch_new
  C1 = Capacitor [package=cap-pth-small-kit]
  R1 = Resistor [tolerance=±5% resistance=200 package=THT]
  PULSE1 = female pin header, 3 pins [form="♀ (female)"]
  PULSE = female pin header, 3 pins [form="♀ (female)"]

nets:
  GND: RESET.1, TrimPot.leg2, NANO.GND, BATT.pin2, INK1.GND, C1.2, R1.Pin_1, PULSE1.pin3, PULSE.pin3
  N1: RESET.3, NANO.RESET
  3V3: TrimPot.leg1, NANO.3V3
  N2: TrimPot.wiper, INK1.LED
  N3: NANO.D2, INK1.CE
  N4: NANO.D3, INK1.RST
  N5: NANO.D4, INK1.DC
  N6: NANO.D5, INK1.DIN
  N7: NANO.D6, INK1.CLK
  N8: NANO.D9, LED_BLINK.pin1
  VIN: NANO.VIN, SW1.pin_2, C1.1
  5V: NANO.5V, INK1.Vcc, PULSE1.pin2, PULSE.pin2
  N9: NANO.A0, PULSE1.pin1, PULSE.pin1
  N10: BATT.pin1, SW1.pin_1
  N11: LED_BLINK.pin2, R1.Pin_0

notes:
  EKG 1, Pulse Monitor, 0
  For Pulse Conc
  Finger

custom parts:
  Nokia 5110: Nokia 5110 INK display
  Slide_Switch_new: the New two pin slide switch
